// Digital circuit datapoint_001.dig as structural Verilog
module datapoint_001 (
  output [7:0] Mem_data
);

  wire Clock_out, Reset_out;
  wire [12:0] u_dp2200_cpu_mem_addr;

  Button Clock (.out(Clock_out));
  Button #(.activeLow("true")) Reset (.out(Reset_out));
  dp2200_cpu #(.applicationType("IVERILOG"), .CodeFile("C:\\Users\\andre\\Downloads\\PROJECTS\\DATAPOINT_2200\\datapoint_2200_fpga\\rtl\\dp2200_cpu.v")) u_dp2200_cpu (
    .clk(Clock_out), .rst_n(Reset_out), .mem_rdata(Mem_data), .mem_addr(u_dp2200_cpu_mem_addr));
  dp2200_rom #(.applicationType("IVERILOG"), .CodeFile("C:\\Users\\andre\\Downloads\\PROJECTS\\DATAPOINT_2200\\datapoint_2200_fpga\\rtl\\dp2200_rom.v")) u_dp2200_rom (
    .clk(Clock_out), .addr(u_dp2200_cpu_mem_addr), .rdata(Mem_data));
endmodule
